// Logisim project Journey_Towards_IRAM.circ as structural Verilog: 4 circuits, main circuit Core_2x2
// Processor
module Core_2x2 (
  input  [15:0] A1,
  input  [15:0] E2,
  input  [15:0] B1,
  input  [15:0] G2,
  input  [15:0] A_1,
  input  [15:0] F2,
  input  [15:0] B_1,
  input  [15:0] H2,
  input  [15:0] C1,
  input  [15:0] E_2,
  input  [15:0] D1,
  input  [15:0] G_2,
  input  [15:0] C_1,
  input  [15:0] F_2,
  input  [15:0] D_1,
  input  [15:0] H_2,
  output [15:0] R1,
  output [15:0] R2,
  output [15:0] R3,
  output [15:0] R4
);

  wire [15:0] multiplier_1_out, multiplier_2_out, multiplier_3_out, multiplier_4_out, multiplier_5_out,
       multiplier_6_out, multiplier_7_out, multiplier_8_out;

  Multiplier #(.width(16)) multiplier_1 (.a(A1), .b(E2), .out(multiplier_1_out));  // open: cin, cout
  Multiplier #(.width(16)) multiplier_2 (.a(B1), .b(G2), .out(multiplier_2_out));  // open: cin, cout
  Multiplier #(.width(16)) multiplier_3 (.a(A_1), .b(F2), .out(multiplier_3_out));  // open: cin, cout
  Multiplier #(.width(16)) multiplier_4 (.a(B_1), .b(H2), .out(multiplier_4_out));  // open: cin, cout
  Multiplier #(.width(16)) multiplier_5 (.a(C1), .b(E_2), .out(multiplier_5_out));  // open: cin, cout
  Multiplier #(.width(16)) multiplier_6 (.a(D1), .b(G_2), .out(multiplier_6_out));  // open: cin, cout
  Multiplier #(.width(16)) multiplier_7 (.a(C_1), .b(F_2), .out(multiplier_7_out));  // open: cin, cout
  Multiplier #(.width(16)) multiplier_8 (.a(D_1), .b(H_2), .out(multiplier_8_out));  // open: cin, cout
  Adder #(.width(16)) adder_1 (.a(multiplier_1_out), .b(multiplier_2_out), .out(R1));  // open: cin, cout
  Adder #(.width(16)) adder_2 (.a(multiplier_3_out), .b(multiplier_4_out), .out(R2));  // open: cin, cout
  Adder #(.width(16)) adder_3 (.a(multiplier_5_out), .b(multiplier_6_out), .out(R3));  // open: cin, cout
  Adder #(.width(16)) adder_4 (.a(multiplier_7_out), .b(multiplier_8_out), .out(R4));  // open: cin, cout
endmodule

module Matrix_Multiplication_2x2 (
  input  in_1,
  input  in_2,
  input  in_3,
  input  in_4,
  input  in_5,
  input  in_6,
  input  in_7,
  input  in_8,
  input  in_9,
  input  in_10,
  input  in_11,
  input  in_12,
  input  in_13
);

  wire and_1_out, CC_out, not_1_out, or_1_out;
  wire [7:0] Address_Counter_q, Clock_Cycle_Counter_q;
  wire [15:0] A1_q, B1_q, C1_q, D1_q, E2_q, F2_q, G2_q, H2_q, R1_out, RAM_A_dout, RAM_B_dout,
       Simplified_Core_r1, Simplified_Core_r2, Simplified_Core_r3, Simplified_Core_r4;

  Counter Address_Counter (.up(1'b1), .clk(CC_out), .Q(Address_Counter_q));  // open: clr, load, count, D, carry
  Clock CC (.out(CC_out));
  not not_1 (not_1_out, and_1_out);
  and and_1 (and_1_out, 1'b1, or_1_out);
  Counter Clock_Cycle_Counter (
    .up(not_1_out), .clk(and_1_out), .Q(Clock_Cycle_Counter_q));  // open: clr, load, count, D, carry
  assign R1_out = in_10 ? Simplified_Core_r1 : 16'bz;  // Controlled_Buffer R1
  assign R1_out = in_11 ? Simplified_Core_r2 : 16'bz;  // Controlled_Buffer R2
  assign R1_out = in_12 ? Simplified_Core_r3 : 16'bz;  // Controlled_Buffer R3
  assign R1_out = in_13 ? Simplified_Core_r4 : 16'bz;  // Controlled_Buffer R4
  or or_1 (or_1_out, in_13, in_12, in_11, in_10);
  RAM #(.dataWidth(16)) RAM_C (
    .addr(Clock_Cycle_Counter_q), .we(in_9), .clk(or_1_out), .din(R1_out));  // open: oe, dout
  RAM #(.dataWidth(16), .\type ("nonvolatile")) RAM_A (
    .addr(Address_Counter_q), .clk(CC_out), .dout(RAM_A_dout));  // open: we, oe, din
  Register #(.width(16)) A1 (.D(RAM_A_dout), .en(in_1), .clk(CC_out), .Q(A1_q));  // open: clr
  Register #(.width(16)) E2 (.D(RAM_B_dout), .en(in_5), .clk(CC_out), .Q(E2_q));  // open: clr
  Register #(.width(16)) B1 (.D(RAM_A_dout), .en(in_2), .clk(CC_out), .Q(B1_q));  // open: clr
  Register #(.width(16)) F2 (.D(RAM_B_dout), .en(in_6), .clk(CC_out), .Q(F2_q));  // open: clr
  Register #(.width(16)) C1 (.D(RAM_A_dout), .en(in_3), .clk(CC_out), .Q(C1_q));  // open: clr
  Register #(.width(16)) G2 (.D(RAM_B_dout), .en(in_7), .clk(CC_out), .Q(G2_q));  // open: clr
  // Probe on Simplified_Core_r1
  // Probe on Simplified_Core_r2
  // Probe on Simplified_Core_r3
  // Probe on Simplified_Core_r4
  Register #(.width(16)) D1 (.D(RAM_A_dout), .en(in_4), .clk(CC_out), .Q(D1_q));  // open: clr
  Register #(.width(16)) H2 (.D(RAM_B_dout), .en(in_8), .clk(CC_out), .Q(H2_q));  // open: clr
  RAM #(.dataWidth(16), .\type ("nonvolatile")) RAM_B (
    .addr(Address_Counter_q), .clk(CC_out), .dout(RAM_B_dout));  // open: we, oe, din
  Core_2x2 Simplified_Core (
    .A1(A1_q), .E2(E2_q), .B1(B1_q), .G2(G2_q), .A_1(A1_q), .F2(F2_q), .B_1(B1_q), .H2(H2_q), .C1(C1_q),
    .E_2(E2_q), .D1(D1_q), .G_2(G2_q), .C_1(C1_q), .F_2(F2_q), .D_1(D1_q), .H_2(H2_q),
    .R1(Simplified_Core_r1), .R2(Simplified_Core_r2), .R3(Simplified_Core_r3), .R4(Simplified_Core_r4));
  RAM #(.dataWidth(16), .\type ("nonvolatile")) Results (
    .addr(Clock_Cycle_Counter_q), .clk(or_1_out));  // open: we, oe, din, dout
endmodule

module ROM_Matrix_Multiplication_2x2 (
);

  wire CC_out, or_1_out;
  wire [3:0] counter_1_q, counter_1_q_2;
  wire [7:0] Address_Counter_q, Clock_Cycle_Counter_q;
  wire [15:0] A1_q, B1_q, C1_q, D1_q, E2_q, F2_q, G2_q, H2_q, R1_out, RAM_A_dout, RAM_B_dout, rom_1_data,
       Simplified_Core_r1, Simplified_Core_r2, Simplified_Core_r3, Simplified_Core_r4;

  Counter Address_Counter (.up(1'b1), .clk(CC_out), .Q(Address_Counter_q));  // open: clr, load, count, D, carry
  Clock CC (.out(CC_out));
  Counter Clock_Cycle_Counter (
    .up(1'b1), .clk(rom_1_data[7]), .Q(Clock_Cycle_Counter_q));  // open: clr, load, count, D, carry
  assign R1_out = rom_1_data[3] ? Simplified_Core_r1 : 16'bz;  // Controlled_Buffer R1
  assign R1_out = rom_1_data[2] ? Simplified_Core_r2 : 16'bz;  // Controlled_Buffer R2
  assign R1_out = rom_1_data[1] ? Simplified_Core_r3 : 16'bz;  // Controlled_Buffer R3
  assign R1_out = rom_1_data[0] ? Simplified_Core_r4 : 16'bz;  // Controlled_Buffer R4
  or or_1 (or_1_out, rom_1_data[0], rom_1_data[1], rom_1_data[2], rom_1_data[3]);
  Register #(.width(16)) A1 (.D(RAM_A_dout), .en(rom_1_data[15]), .clk(CC_out), .Q(A1_q));  // open: clr
  Register #(.width(16)) E2 (.D(RAM_B_dout), .en(rom_1_data[11]), .clk(CC_out), .Q(E2_q));  // open: clr
  RAM #(.dataWidth(16)) RAM_C (
    .addr(Clock_Cycle_Counter_q), .we(rom_1_data[4]), .clk(or_1_out), .din(R1_out));  // open: oe, dout
  RAM #(.dataWidth(16), .\type ("nonvolatile")) RAM_A (
    .addr(Address_Counter_q), .clk(CC_out), .dout(RAM_A_dout));  // open: we, oe, din
  Register #(.width(16)) B1 (.D(RAM_A_dout), .en(rom_1_data[14]), .clk(CC_out), .Q(B1_q));  // open: clr
  Register #(.width(16)) F2 (.D(RAM_B_dout), .en(rom_1_data[10]), .clk(CC_out), .Q(F2_q));  // open: clr
  Register #(.width(16)) C1 (.D(RAM_A_dout), .en(rom_1_data[13]), .clk(CC_out), .Q(C1_q));  // open: clr
  Register #(.width(16)) G2 (.D(RAM_B_dout), .en(rom_1_data[9]), .clk(CC_out), .Q(G2_q));  // open: clr
  // Probe on Simplified_Core_r1
  // Probe on Simplified_Core_r2
  // Probe on Simplified_Core_r3
  // Probe on Simplified_Core_r4
  Register #(.width(16)) D1 (.D(RAM_A_dout), .en(rom_1_data[12]), .clk(CC_out), .Q(D1_q));  // open: clr
  Register #(.width(16)) H2 (.D(RAM_B_dout), .en(rom_1_data[8]), .clk(CC_out), .Q(H2_q));  // open: clr
  RAM #(.dataWidth(16), .\type ("nonvolatile")) RAM_B (
    .addr(Address_Counter_q), .clk(CC_out), .dout(RAM_B_dout));  // open: we, oe, din
  Core_2x2 Simplified_Core (
    .A1(A1_q), .E2(E2_q), .B1(B1_q), .G2(G2_q), .A_1(A1_q), .F2(F2_q), .B_1(B1_q), .H2(H2_q), .C1(C1_q),
    .E_2(E2_q), .D1(D1_q), .G_2(G2_q), .C_1(C1_q), .F_2(F2_q), .D_1(D1_q), .H_2(H2_q),
    .R1(Simplified_Core_r1), .R2(Simplified_Core_r2), .R3(Simplified_Core_r3), .R4(Simplified_Core_r4));
  RAM #(.dataWidth(16), .\type ("nonvolatile")) Results (
    .addr(Clock_Cycle_Counter_q), .clk(or_1_out));  // open: we, oe, din, dout
  Counter counter_1 (.clk(CC_out), .Q({counter_1_q_2, counter_1_q}));  // open: clr, load, up, count, D, carry
  Hex_Digit_Display hex_digit_display_1 (.value(counter_1_q_2));  // open: dp
  Hex_Digit_Display hex_digit_display_2 (.value(counter_1_q));  // open: dp
  ROM #(.dataWidth(16)) rom_1 (.addr({counter_1_q_2, counter_1_q}), .data(rom_1_data));

  // Notes on the sheet:
  //   contents of rom_1 (hex, n*v repeats v):
  //   0 8800 4400 2200 1100 18 80 14 80 12 80 11
  //   15) A1
  //   14) B1
  //   13) C1
  //   12) D2
  //   11) E2
  //   10) F2
  //   9) G2
  //   8) H2
  //   7) Address Increase
  //   4) WE of RAM C
endmodule

module IRAM_Matrix_Multiplication_2x2 (
);

  wire and_1_out, and_2_out, CC_out, not_1_out, not_2_out, not_3_out, or_1_out;
  wire [3:0] Program_Counter_q, Program_Counter_q_2;
  wire [7:0] Address_Counter_q, Clock_Cycle_Counter_q;
  wire [15:0] A1_q, B1_q, C1_q, D1_q, E2_q, F2_q, G2_q, H2_q, Instruction_RAM_dout, R1_out, RAM_A_dout,
       RAM_B_dout, Simplified_Core_r1, Simplified_Core_r2, Simplified_Core_r3, Simplified_Core_r4;

  and and_1 (and_1_out, 1'b1, or_1_out);
  Counter Address_Counter (.count(1'b1), .clk(CC_out), .Q(Address_Counter_q));  // open: clr, load, up, D, carry
  Clock CC (.out(CC_out));
  Counter Clock_Cycle_Counter (
    .up(1'b1), .clk(and_1_out), .Q(Clock_Cycle_Counter_q));  // open: clr, load, count, D, carry
  assign R1_out = Instruction_RAM_dout[12] ? Simplified_Core_r1 : 16'bz;  // Controlled_Buffer R1
  assign R1_out = Instruction_RAM_dout[13] ? Simplified_Core_r2 : 16'bz;  // Controlled_Buffer R2
  assign R1_out = Instruction_RAM_dout[14] ? Simplified_Core_r3 : 16'bz;  // Controlled_Buffer R3
  assign R1_out = Instruction_RAM_dout[15] ? Simplified_Core_r4 : 16'bz;  // Controlled_Buffer R4
  or or_1 (or_1_out, Instruction_RAM_dout[15], Instruction_RAM_dout[14], Instruction_RAM_dout[13], Instruction_RAM_dout[12]);
  Register #(.width(16)) A1 (.D(RAM_A_dout), .en(Instruction_RAM_dout[4]), .clk(CC_out), .Q(A1_q));  // open: clr
  Register #(.width(16)) E2 (.D(RAM_B_dout), .en(Instruction_RAM_dout[8]), .clk(CC_out), .Q(E2_q));  // open: clr
  RAM #(.dataWidth(16)) RAM_C (
    .addr(Clock_Cycle_Counter_q), .we(1'b1), .clk(or_1_out), .din(R1_out));  // open: oe, dout
  RAM #(.dataWidth(16), .\type ("nonvolatile")) RAM_A (
    .addr(Address_Counter_q), .clk(CC_out), .dout(RAM_A_dout));  // open: we, oe, din
  Register #(.width(16)) B1 (.D(RAM_A_dout), .en(Instruction_RAM_dout[5]), .clk(CC_out), .Q(B1_q));  // open: clr
  Register #(.width(16)) F2 (.D(RAM_B_dout), .en(Instruction_RAM_dout[9]), .clk(CC_out), .Q(F2_q));  // open: clr
  Register #(.width(16)) C1 (.D(RAM_A_dout), .en(Instruction_RAM_dout[6]), .clk(CC_out), .Q(C1_q));  // open: clr
  Register #(.width(16)) G2 (.D(RAM_B_dout), .en(Instruction_RAM_dout[10]), .clk(CC_out), .Q(G2_q));  // open: clr
  // Probe on Simplified_Core_r1
  // Probe on Simplified_Core_r2
  // Probe on Simplified_Core_r3
  // Probe on Simplified_Core_r4
  Register #(.width(16)) D1 (.D(RAM_A_dout), .en(Instruction_RAM_dout[7]), .clk(CC_out), .Q(D1_q));  // open: clr
  Register #(.width(16)) H2 (.D(RAM_B_dout), .en(Instruction_RAM_dout[11]), .clk(CC_out), .Q(H2_q));  // open: clr
  RAM #(.dataWidth(16), .\type ("nonvolatile")) RAM_B (
    .addr(Address_Counter_q), .clk(CC_out), .dout(RAM_B_dout));  // open: we, oe, din
  Core_2x2 Simplified_Core (
    .A1(A1_q), .E2(E2_q), .B1(B1_q), .G2(G2_q), .A_1(A1_q), .F2(F2_q), .B_1(B1_q), .H2(H2_q), .C1(C1_q),
    .E_2(E2_q), .D1(D1_q), .G_2(G2_q), .C_1(C1_q), .F_2(F2_q), .D_1(D1_q), .H_2(H2_q),
    .R1(Simplified_Core_r1), .R2(Simplified_Core_r2), .R3(Simplified_Core_r3), .R4(Simplified_Core_r4));
  RAM #(.dataWidth(16), .\type ("nonvolatile")) Results (
    .addr(Clock_Cycle_Counter_q), .clk(or_1_out));  // open: we, oe, din, dout
  Counter Program_Counter (
    .up(1'b1), .clk(CC_out), .Q({Program_Counter_q_2, Program_Counter_q}));  // open: clr, load, count, D, carry
  Hex_Digit_Display hex_digit_display_1 (.value(Program_Counter_q_2));  // open: dp
  Hex_Digit_Display hex_digit_display_2 (.value(Program_Counter_q));  // open: dp
  RAM #(.dataWidth(16), .\type ("nonvolatile")) Instruction_RAM (
    .addr({Program_Counter_q_2, Program_Counter_q}), .clk(CC_out), .dout(Instruction_RAM_dout));  // open: we, oe, din
  not not_1 (not_1_out, Instruction_RAM_dout[1]);
  not not_2 (not_2_out, Instruction_RAM_dout[2]);
  not not_3 (not_3_out, Instruction_RAM_dout[3]);
  and and_2 (and_2_out, Instruction_RAM_dout[0], not_1_out, not_2_out, not_3_out);
  // Probe on and_2_out

  // Notes on the sheet:
  //   OP CODE
  //   Operand
endmodule
